// Logisim project final.circ as structural Verilog: 1 circuit, main circuit main
module main (
  input  in_1,
  input  in_2,
  input  [3:0] in_3,
  input  in_4,
  input  [3:0] in_5,
  input  [3:0] in_6,
  input  [3:0] Right_Shift_EAQ,
  input  in_8,
  input  [2:0] in_9,
  input  [2:0] in_10,
  input  in_11,
  output out_12,
  output [8:0] out_13,
  output out_14,
  output [8:0] out_15,
  output [8:0] out_16,
  output [8:0] out_17,
  output [8:0] out_18,
  output [8:0] out_19,
  output [8:0] out_20,
  output out_21,
  output [3:0] Q,
  output [3:0] A
);

  wire adder_1_cout, and_1_out, clock_1_out, clock_2_out, not_1_out;
  wire [2:0] counter_1_q;
  wire [3:0] adder_1_out, controlled_buffer_1_out, controlled_buffer_2_out, multiplexer_1_out, register_2_q,
       register_3_q;
  wire [3:1] register_1_q;

  Clock clock_1 (.out(clock_1_out));
  Register #(.width(4)) register_1 (
    .D(controlled_buffer_1_out), .Q({register_1_q, out_12}), .clk(clock_1_out));  // open: en, clr
  Register #(.width(4)) register_2 (.D(controlled_buffer_2_out), .Q(register_2_q), .clk(clock_1_out));  // open: en, clr
  assign out_15 = {{5{1'b0}}, {register_1_q, out_12}};  // Bit_Extender bit_extender_1
  Clock clock_2 (.out(clock_2_out));
  Register #(.width(4)) register_3 (.D(in_3), .Q(register_3_q), .clk(in_4));  // open: en, clr
  Counter #(.width(3), .max('h7)) counter_1 (
    .load(in_8), .D(in_9), .count(in_11), .Q(counter_1_q), .clk(clock_2_out));  // open: carry, clr
  Adder #(.width(4)) adder_1 (.a(register_2_q), .b(register_3_q), .out(adder_1_out), .cout(adder_1_cout));  // open: cin
  and and_1 (and_1_out, out_12, adder_1_cout);
  assign out_16 = {{8{1'b0}}, and_1_out};  // Bit_Extender bit_extender_2
  Comparator #(.width(3)) comparator_1 (.a(counter_1_q), .b(in_10), .eq(out_21));  // open: gt, lt
  Multiplexer #(.width(4), .enable("false")) multiplexer_1 (
    .in0(register_2_q), .in1(adder_1_out), .out(multiplexer_1_out), .sel(out_12));
  Shifter #(.width(9), .shift("rr")) shifter_1 (.in(out_16), .\dist (in_6), .out(out_18));
  not not_1 (not_1_out, out_21);
  assign controlled_buffer_1_out = not_1_out ? out_20[3:0] : 4'bz;  // Controlled_Buffer controlled_buffer_1
  assign out_19 = out_18 | out_17 | out_15;  // OR_Gate or_1, 9 bits wide
  assign controlled_buffer_2_out = not_1_out ? A : 4'bz;  // Controlled_Buffer controlled_buffer_2
  assign out_13 = {{5{1'b0}}, multiplexer_1_out};  // Bit_Extender bit_extender_3
  Shifter #(.width(9), .shift("lr")) shifter_2 (
    .in(out_19), .\dist (Right_Shift_EAQ), .out({out_20[8], A, out_20[3:0]}));
  Shifter #(.width(9), .shift("rr")) shifter_3 (.in(out_13), .\dist (in_5), .out(out_17));
  Register #(.width(9)) register_4 (.D({out_20[8], A, out_20[3:0]}), .clk(clock_2_out));  // open: en, Q, clr
  xor xor_1 (out_14, in_1, in_2);

  assign out_20[7:4] = A;
  assign Q = out_20[3:0];

  // Notes on the sheet:
  //   Q
  //   A
  //   bit Extender
  //   B
  //   E
  //   Bit Extender
  //   Q
  //   E
  //   A
  //   EAQ
  //   Bit Extender
  //   Bit shifter
endmodule
