// Logisim project Multiplier.circ as structural Verilog: 2 circuits, main circuit main
module main (
  input  _0,
  input  _1,
  input  _2,
  input  _3,
  input  _4,
  input  _5,
  input  _6,
  input  _7,
  input  _8,
  input  _9,
  input  _10,
  input  _11,
  input  _12,
  input  _13,
  input  _14,
  input  _15,
  input  _0_2,
  input  _1_2,
  input  _2_2,
  input  _3_2,
  input  _4_2,
  input  _5_2,
  input  _6_2,
  input  _7_2,
  input  _8_2,
  input  _9_2,
  input  _10_2,
  input  _11_2,
  input  _12_2,
  input  _13_2,
  input  _14_2,
  input  _15_2,
  input  D,
  input  C,
  input  D_2,
  input  B,
  input  C_2,
  input  B_2,
  output [7:0] out_39
);

  wire A0, A0_B1_out, A0_B2_out, A0_B3_out, A1, A1_B0_out, A1_B1_out, A1_B2_out, A1_B3_out, A2, A2_B0_out,
       A2_B1_out, A2_B2_out, A2_B3_2_out, A2_B3_out, A2A1_out, A3, A3_B0_out, A3_B1_out, A3_B2_out,
       A3_prime_A1_out, A3_prime_A2_out, A3A1_out, A3A2_out, A3A2_prime_A1_prime_out, A3A2A1_prime_out,
       adder_1_cout, adder_2_cout, adder_2_out, adder_3_cout, adder_3_out, adder_4_cout, adder_4_out,
       adder_5_cout, adder_6_cout, adder_6_out, adder_7_cout, adder_7_out, adder_8_cout, adder_8_out,
       adder_9_cout, adder_10_cout, adder_11_cout, B0, B1, B2, B3, B3_prime_B1_out, B3_prime_B2_out,
       B3B1_out, B3B2_out, B3B2_prime_B1_prime_out, B3B2B1_prime_2_out, B3B2B1_prime_out,
       binary_to_decimal_1_a_2, binary_to_decimal_1_b_2, binary_to_decimal_1_c_2, binary_to_decimal_1_d_2,
       binary_to_decimal_1_e, binary_to_decimal_1_f, binary_to_decimal_1_g, binary_to_decimal_2_a_2,
       binary_to_decimal_2_b_2, binary_to_decimal_2_c_2, binary_to_decimal_2_d_2, binary_to_decimal_2_e,
       binary_to_decimal_2_f, binary_to_decimal_2_g, binary_to_decimal_3_a_2, binary_to_decimal_3_b_2,
       binary_to_decimal_3_c_2, binary_to_decimal_3_d_2, binary_to_decimal_3_e, binary_to_decimal_3_f,
       binary_to_decimal_3_g, binary_to_decimal_4_a_2, binary_to_decimal_4_b_2, binary_to_decimal_4_c_2,
       binary_to_decimal_4_d_2, binary_to_decimal_4_e, binary_to_decimal_4_f, binary_to_decimal_4_g,
       not_1_out, not_2_out, not_3_out, not_5_out, not_6_out, not_7_out, or_1_out, or_2_out, or_3_out,
       or_4_out, or_5_out, or_6_out;

  and A0_B0 (out_39[0], A0, B0);
  and A1_B0 (A1_B0_out, A1, B0);
  and A2_B0 (A2_B0_out, A2, B0);
  and A3_B0 (A3_B0_out, A3, B0);
  or u_A3 (A3, _8, _9, _10, _11, _12, _13, _14, _15);
  or u_A2 (A2, _4, _5, _6, _7, _12, _13, _14, _15);
  or u_A1 (A1, _2, _3, _6, _7, _10, _11, _14, _15);
  or u_A0 (A0, _1, _3, _5, _7, _9, _11, _13, _15);
  and A0_B1 (A0_B1_out, A0, B1);
  and A1_B1 (A1_B1_out, A1, B1);
  and A2_B1 (A2_B1_out, A2, B1);
  and A3_B1 (A3_B1_out, A3, B1);
  Adder #(.width(1)) adder_1 (.a(A1_B0_out), .b(A0_B1_out), .out(out_39[1]), .cin(1'b0), .cout(adder_1_cout));
  Adder #(.width(1)) adder_2 (.a(A2_B0_out), .b(A1_B1_out), .out(adder_2_out), .cin(adder_1_cout), .cout(adder_2_cout));
  Adder #(.width(1)) adder_3 (.a(A3_B0_out), .b(A2_B1_out), .out(adder_3_out), .cin(adder_2_cout), .cout(adder_3_cout));
  Adder #(.width(1)) adder_4 (.a(adder_3_cout), .b(A3_B1_out), .out(adder_4_out), .cin(1'b0), .cout(adder_4_cout));
  not not_1 (not_1_out, A3);
  not not_2 (not_2_out, A2);
  not not_3 (not_3_out, A1);
  and A0_B2 (A0_B2_out, A0, B2);
  and A1_B2 (A1_B2_out, A1, B2);
  and A2_B2 (A2_B2_out, A2, B2);
  and A3_B2 (A3_B2_out, A3, B2);
  // NOT_Gate not_4 has open pins: in=A0, out=open
  Adder #(.width(1)) adder_5 (.a(adder_2_out), .b(A0_B2_out), .out(out_39[2]), .cin(1'b0), .cout(adder_5_cout));
  Adder #(.width(1)) adder_6 (
    .a(adder_3_out), .b(A1_B2_out), .out(adder_6_out), .cin(adder_5_cout), .cout(adder_6_cout));
  Adder #(.width(1)) adder_7 (
    .a(adder_4_out), .b(A2_B2_out), .out(adder_7_out), .cin(adder_6_cout), .cout(adder_7_cout));
  Adder #(.width(1)) adder_8 (
    .a(adder_4_cout), .b(A3_B2_out), .out(adder_8_out), .cin(adder_7_cout), .cout(adder_8_cout));
  and A3_prime_A1 (A3_prime_A1_out, not_1_out, A1);
  and A3A2A1_prime (A3A2A1_prime_out, A3, A2, not_3_out);
  and A2A1 (A2A1_out, A2, A1);
  and A3_prime_A2 (A3_prime_A2_out, not_1_out, A2);
  and A3A2_prime_A1_prime (A3A2_prime_A1_prime_out, A3, not_2_out, not_3_out);
  and A3A2 (A3A2_out, A3, A2);
  and A3A1 (A3A1_out, A3, A1);
  and A0_B3 (A0_B3_out, A0, B3);
  and A1_B3 (A1_B3_out, A1, B3);
  and A2_B3 (A2_B3_out, A2, B3);
  and A2_B3_2 (A2_B3_2_out, A3, B3);
  or or_1 (or_1_out, A3_prime_A1_out, A3A2A1_prime_out);
  or or_2 (or_2_out, A2A1_out, A3_prime_A2_out);
  or or_3 (or_3_out, A3A2_out, A3A1_out);
  Adder #(.width(1)) adder_9 (.a(adder_6_out), .b(A0_B3_out), .out(out_39[3]), .cin(1'b0), .cout(adder_9_cout));
  Adder #(.width(1)) adder_10 (
    .a(adder_7_out), .b(A1_B3_out), .out(out_39[4]), .cin(adder_9_cout), .cout(adder_10_cout));
  Adder #(.width(1)) adder_11 (
    .a(adder_8_out), .b(A2_B3_out), .out(out_39[5]), .cin(adder_10_cout), .cout(adder_11_cout));
  Adder #(.width(1)) adder_12 (
    .a(adder_8_cout), .b(A2_B3_2_out), .out(out_39[6]), .cin(adder_11_cout), .cout(out_39[7]));
  binary_to_decimal binary_to_decimal_1 (
    .D(D), .C(C), .B(B), .A(or_3_out), .a_2(binary_to_decimal_1_a_2), .b_2(binary_to_decimal_1_b_2),
    .c_2(binary_to_decimal_1_c_2), .d_2(binary_to_decimal_1_d_2), .e(binary_to_decimal_1_e),
    .f(binary_to_decimal_1_f), .g(binary_to_decimal_1_g));
  _7_Segment_Display u_7_segment_display_1 (
    .g(binary_to_decimal_1_g), .f(binary_to_decimal_1_f), .a(binary_to_decimal_1_a_2),
    .b(binary_to_decimal_1_b_2), .e(binary_to_decimal_1_e), .d(binary_to_decimal_1_d_2),
    .c(binary_to_decimal_1_c_2));  // open: dp
  _7_Segment_Display u_7_segment_display_2 (
    .g(binary_to_decimal_2_g), .f(binary_to_decimal_2_f), .a(binary_to_decimal_2_a_2),
    .b(binary_to_decimal_2_b_2), .e(binary_to_decimal_2_e), .d(binary_to_decimal_2_d_2),
    .c(binary_to_decimal_2_c_2));  // open: dp
  binary_to_decimal binary_to_decimal_2 (
    .D(A3A2_prime_A1_prime_out), .C(or_2_out), .B(or_1_out), .A(A0), .a_2(binary_to_decimal_2_a_2),
    .b_2(binary_to_decimal_2_b_2), .c_2(binary_to_decimal_2_c_2), .d_2(binary_to_decimal_2_d_2),
    .e(binary_to_decimal_2_e), .f(binary_to_decimal_2_f), .g(binary_to_decimal_2_g));
  or u_B3 (B3, _8_2, _9_2, _10_2, _11_2, _12_2, _13_2, _14_2, _15_2);
  or u_B2 (B2, _4_2, _5_2, _6_2, _7_2, _12_2, _13_2, _14_2, _15_2);
  or u_B1 (B1, _2_2, _3_2, _6_2, _7_2, _10_2, _11_2, _14_2, _15_2);
  or u_B0 (B0, _1_2, _3_2, _5_2, _7_2, _9_2, _11_2, _13_2, _15_2);
  not not_5 (not_5_out, B3);
  not not_6 (not_6_out, B2);
  not not_7 (not_7_out, B1);
  // NOT_Gate not_8 has open pins: in=B0, out=open
  and B3_prime_B1 (B3_prime_B1_out, not_5_out, B1);
  and B3B2B1_prime (B3B2B1_prime_out, B3, B2, not_7_out);
  and B3B2B1_prime_2 (B3B2B1_prime_2_out, B2, B1);
  and B3_prime_B2 (B3_prime_B2_out, not_5_out, B2);
  and B3B2_prime_B1_prime (B3B2_prime_B1_prime_out, B3, not_6_out, not_7_out);
  and B3B2 (B3B2_out, B3, B2);
  and B3B1 (B3B1_out, B3, B1);
  or or_4 (or_4_out, B3_prime_B1_out, B3B2B1_prime_out);
  or or_5 (or_5_out, B3B2B1_prime_2_out, B3_prime_B2_out);
  or or_6 (or_6_out, B3B2_out, B3B1_out);
  binary_to_decimal binary_to_decimal_3 (
    .D(D_2), .C(C_2), .B(B_2), .A(or_6_out), .a_2(binary_to_decimal_3_a_2), .b_2(binary_to_decimal_3_b_2),
    .c_2(binary_to_decimal_3_c_2), .d_2(binary_to_decimal_3_d_2), .e(binary_to_decimal_3_e),
    .f(binary_to_decimal_3_f), .g(binary_to_decimal_3_g));
  _7_Segment_Display u_7_segment_display_3 (
    .g(binary_to_decimal_3_g), .f(binary_to_decimal_3_f), .a(binary_to_decimal_3_a_2),
    .b(binary_to_decimal_3_b_2), .e(binary_to_decimal_3_e), .d(binary_to_decimal_3_d_2),
    .c(binary_to_decimal_3_c_2));  // open: dp
  _7_Segment_Display u_7_segment_display_4 (
    .g(binary_to_decimal_4_g), .f(binary_to_decimal_4_f), .a(binary_to_decimal_4_a_2),
    .b(binary_to_decimal_4_b_2), .e(binary_to_decimal_4_e), .d(binary_to_decimal_4_d_2),
    .c(binary_to_decimal_4_c_2));  // open: dp
  binary_to_decimal binary_to_decimal_4 (
    .D(B3B2_prime_B1_prime_out), .C(or_5_out), .B(or_4_out), .A(B0), .a_2(binary_to_decimal_4_a_2),
    .b_2(binary_to_decimal_4_b_2), .c_2(binary_to_decimal_4_c_2), .d_2(binary_to_decimal_4_d_2),
    .e(binary_to_decimal_4_e), .f(binary_to_decimal_4_f), .g(binary_to_decimal_4_g));

  // Other names for the same wires on the sheet: P0 = out_39[0]; P1 = out_39[1]; P2 = out_39[2]; P3 = out_39[3];
  //   P4 = out_39[4]; P5 = out_39[5]; P6 = out_39[6]; P7 = out_39[7]

  // Notes on the sheet:
  //   INPUT
  //   ENCODER
  //   MULTIPLIER CICUIT
  //   BINARY TO BCD
  //   7-SEGMENT DISPLAY (BINARY TO DECIMAL)
  //   INPUT
  //   ENCODER
  //   BINARY TO BCD
  //   OUTPUT
  //   7-SEGMENT DISPLAY (BINARY TO DECIMAL)
  //   OUTPUT
endmodule

module binary_to_decimal (
  input  D,
  input  C,
  input  B,
  input  A,
  output a_2,
  output b_2,
  output c_2,
  output d_2,
  output e,
  output f,
  output g
);

  wire and_1_out, and_2_out, and_3_out, and_4_out, and_5_out, and_6_out, and_7_out, and_8_out, and_9_out,
       and_10_out, and_11_out, and_12_out, and_13_out, and_14_out, and_15_out, and_16_out, not_1_out,
       not_2_out, not_3_out, not_4_out, not_5_out, not_6_out, not_7_out, not_8_out, not_9_out, not_10_out,
       not_11_out, not_12_out, not_13_out, not_14_out, not_15_out, not_16_out, not_17_out, not_18_out,
       not_19_out, not_20_out, not_21_out;

  not not_1 (not_1_out, C);
  and and_1 (and_1_out, not_1_out, not_2_out);
  not not_2 (not_2_out, A);
  and and_2 (and_2_out, C, A);
  not not_3 (not_3_out, C);
  not not_4 (not_4_out, B);
  and and_3 (and_3_out, not_4_out, not_5_out);
  not not_5 (not_5_out, A);
  and and_4 (and_4_out, B, A);
  not not_6 (not_6_out, B);
  or or_1 (c_2, not_6_out, A, C);
  not not_7 (not_7_out, C);
  and and_5 (and_5_out, not_7_out, not_8_out);
  not not_8 (not_8_out, A);
  not not_9 (not_9_out, C);
  and and_6 (and_6_out, not_9_out, B);
  and and_7 (and_7_out, B, not_10_out);
  not not_10 (not_10_out, A);
  and and_8 (and_8_out, C, not_11_out, A);
  not not_11 (not_11_out, B);
  not not_12 (not_12_out, C);
  and and_9 (and_9_out, not_12_out, not_13_out);
  not not_13 (not_13_out, A);
  and and_10 (and_10_out, B, not_14_out);
  not not_14 (not_14_out, A);
  not not_15 (not_15_out, B);
  and and_11 (and_11_out, not_15_out, not_16_out);
  not not_16 (not_16_out, A);
  and and_12 (and_12_out, C, not_17_out);
  not not_17 (not_17_out, B);
  and and_13 (and_13_out, C, not_18_out);
  not not_18 (not_18_out, A);
  not not_19 (not_19_out, C);
  and and_14 (and_14_out, not_19_out, B);
  and and_15 (and_15_out, C, not_20_out);
  not not_20 (not_20_out, B);
  and and_16 (and_16_out, C, not_21_out);
  not not_21 (not_21_out, A);
  or or_2 (a_2, and_1_out, B, and_2_out, D);
  or or_3 (b_2, not_3_out, and_3_out, and_4_out);
  or or_4 (d_2, and_5_out, and_6_out, and_7_out, and_8_out, D);
  or or_5 (e, and_9_out, and_10_out);
  or or_6 (f, and_11_out, and_12_out, and_13_out, D);
  or or_7 (g, and_14_out, and_15_out, and_16_out, D);
endmodule
